// Logisim project CMP.circ as structural Verilog: 1 circuit, main circuit main
// CMP
module main (
  input  LT,
  input  EQ,
  input  GT,
  input  [2:0] CQ_QUERY,
  input  CR_WRITE,
  input  CLOCK,
  output [2:0] CR_VAL,
  output CQ_PASSED
);

  wire MUX_OUT, not_1_out, or_1_out, or_2_out;

  Multiplexer #(.select(2)) multiplexer_1 (.in0(LT), .in2(EQ), .in3(GT));  // open: in1, out, sel, en
  Register #(.width(3)) CQ_Register (.D({3{MUX_OUT}}), .en(CR_WRITE), .Q(CR_VAL), .clk(CLOCK));  // open: clr
  or or_1 (or_1_out, EQ, GT);
  not not_1 (not_1_out, EQ);
  or or_2 (or_2_out, EQ, LT);
  Multiplexer #(.select(3), .enable("false")) multiplexer_2 (
    .in0(1'b0), .in1(GT), .in2(EQ), .in3(or_1_out), .in4(LT), .in5(not_1_out), .in6(or_2_out), .in7(1'b1),
    .out(MUX_OUT), .sel(CQ_QUERY));

  // Other names for the same wires on the sheet: clk = CLOCK; tunnel = LT; tunnel_t = EQ; tunnel_t_t = GT

  // Notes on the sheet:
  //   CR MODULE
endmodule
