// Logisim project CPU.circ as structural Verilog: 1 circuit, main circuit main
// CPU
module main (
  input  [31:0] INSTRUCTION,
  input  [23:0] CURRENT_PC,
  input  CQ_PASSED,
  input  [31:0] REG_1_VAL,
  input  [31:0] REG_2_VAL,
  input  [31:0] REG_3_VAL,
  input  [31:0] ALU_RESULT,
  input  [31:0] MEM_OUT,
  output [23:0] JUMP_ADDRESS,
  output [2:0] CQ_QUERY,
  output CR_WRITE,
  output [3:0] REG_1_READ,
  output [3:0] REG_2_READ,
  output [3:0] REG_3_WRITE,
  output [31:0] REG_WRITE_VAL,
  output REG_WRITE,
  output [31:0] ALU_SOURCE_X,
  output [31:0] ALU_SOURCE_Y,
  output [3:0] ALU_OPERATION,
  output [23:0] MEM_ADDR,
  output [31:0] MEM_IN,
  output MEM_WRITE,
  output SHL,
  output SHR,
  output AND,
  output IOR,
  output XOR,
  output STU,
  output MUL,
  output DIV,
  output SUB,
  output ADD,
  output MLD,
  output MST,
  output STL,
  output CMP,
  output LNK,
  output JMP
);

  wire ALUctr_0_out, ALUctr_1_out, ALUSrc_out, clk, comparator_1_eq, comparator_2_eq, comparator_3_eq,
       comparator_4_eq, comparator_6_eq, comparator_7_lt, CQ_Cmd, CQ_Output, ExtOp_out, Jump_Cmd, Link_Cmd,
       Load_Cmd, MemtoReg_out, memWrite, not_2_out, not_3_out, not_4_out, not_5_out, nPC_sel_out, or_1_out,
       prev_jump, RegDst_out, RegWrite_out, write;
  wire [1:0] A_Type;
  wire [31:0] shifter_1_out;

  Shifter #(.width(32), .shift("lr")) shifter_1 (.in(INSTRUCTION), .\dist (5'b11100), .out(shifter_1_out));
  Bit_Extender #(.in_width(32), .out_width(4)) bit_extender_1 (.in(shifter_1_out), .out(ALU_OPERATION));
  Multiplexer #(.width(32), .enable("false")) multiplexer_1 (
    .in0(REG_1_VAL), .in1(REG_2_VAL), .out(ALU_SOURCE_X), .sel(ALUSrc_out));
  Demultiplexer demultiplexer_1 ();  // open: out0, out1, in, sel, en
  Multiplexer #(.width(32), .enable("false")) multiplexer_2 (
    .in0(REG_2_VAL), .in1(REG_1_VAL), .out(ALU_SOURCE_Y), .sel(ALUSrc_out));
  Demultiplexer #(.width(32)) demultiplexer_2 (
    .out0(REG_WRITE_VAL), .in(ALU_RESULT), .sel(RegDst_out));  // open: out1, en
  Comparator #(.width(4), .mode("unsigned")) comparator_1 (
    .a(ALU_OPERATION), .b(4'b1111), .eq(comparator_1_eq));  // open: gt, lt
  Comparator #(.width(4), .mode("unsigned")) comparator_2 (
    .a(ALU_OPERATION), .b(4'b1010), .eq(comparator_2_eq));  // open: gt, lt
  Comparator #(.width(4), .mode("unsigned")) comparator_3 (
    .a(ALU_OPERATION), .b(4'b1011), .eq(comparator_3_eq));  // open: gt, lt
  or ALUSrc (ALUSrc_out, STU, SUB, STL, LNK);
  or RegWrite (RegWrite_out, MST, CMP, JMP);
  not not_1 (REG_WRITE, RegWrite_out);
  // OR_Gate nPC_sel has open pins: out=nPC_sel_out
  // OR_Gate ExtOp has open pins: out=ExtOp_out
  // OR_Gate ALUctr_0 has open pins: out=ALUctr_0_out
  // OR_Gate ALUctr_1 has open pins: out=ALUctr_1_out
  and and_1 (Jump_Cmd, comparator_1_eq, prev_jump, CQ_Output);
  and and_2 (Load_Cmd, comparator_2_eq, prev_jump, CQ_Output);
  and and_3 (memWrite, comparator_3_eq, prev_jump, CQ_Output);
  not not_2 (not_2_out, ALU_OPERATION[0]);
  not not_3 (not_3_out, ALU_OPERATION[1]);
  not not_4 (not_4_out, ALU_OPERATION[2]);
  not not_5 (not_5_out, ALU_OPERATION[3]);
  or RegDst (RegDst_out, MST, CMP);
  buf u_MemWrite (MEM_WRITE, MST);  // OR_Gate
  buf MemtoReg (MemtoReg_out, MLD);  // OR_Gate
  Comparator #(.width(32)) comparator_4 (.a(32'hf), .eq(comparator_4_eq));  // open: b, gt, lt
  and u_SHL (SHL, not_2_out, not_3_out, not_4_out, not_5_out);
  and AND_4 (AND, not_2_out, ALU_OPERATION[0], not_4_out, not_5_out);
  and u_SHR (SHR, ALU_OPERATION[0], not_3_out, not_4_out, not_5_out);
  and u_IOR (IOR, ALU_OPERATION[0], ALU_OPERATION[1], not_4_out, not_5_out);
  Comparator #(.width(4), .mode("unsigned")) comparator_5 (
    .a(ALU_OPERATION), .b(4'b1110), .eq(Link_Cmd));  // open: gt, lt
  and u_XOR (XOR, not_2_out, not_3_out, ALU_OPERATION[2], not_5_out);
  Comparator #(.width(2)) comparator_6 (.a(2'b01), .b(A_Type), .eq(comparator_6_eq));  // open: gt, lt
  Comparator #(.width(4), .mode("unsigned")) comparator_7 (
    .a(ALU_OPERATION), .b(4'b1011), .lt(comparator_7_lt));  // open: gt, eq
  and u_STU (STU, ALU_OPERATION[0], not_4_out, ALU_OPERATION[2], not_5_out);
  and and_5 (CQ_Cmd, comparator_6_eq, prev_jump, CQ_Output);
  or or_1 (or_1_out, comparator_7_lt, Link_Cmd);
  and u_MUL (MUL, not_2_out, ALU_OPERATION[1], ALU_OPERATION[2], not_5_out);
  and and_6 (write, CQ_Output, prev_jump, clk, or_1_out);
  and u_DIV (DIV, ALU_OPERATION[0], ALU_OPERATION[1], ALU_OPERATION[2], not_5_out);
  and u_SUB (SUB, not_2_out, not_3_out, not_4_out, ALU_OPERATION[3]);
  and u_MLD (MLD, not_2_out, ALU_OPERATION[1], not_4_out, ALU_OPERATION[3]);
  and u_ADD (ADD, ALU_OPERATION[0], not_3_out, not_4_out, ALU_OPERATION[3]);
  and u_MST (MST, ALU_OPERATION[0], not_3_out, not_4_out, ALU_OPERATION[3]);
  and u_STL (STL, not_2_out, not_4_out, ALU_OPERATION[2], ALU_OPERATION[3]);
  and u_CMP (CMP, ALU_OPERATION[0], not_3_out, ALU_OPERATION[2], ALU_OPERATION[3]);
  and u_LNK (LNK, not_2_out, ALU_OPERATION[1], ALU_OPERATION[2], ALU_OPERATION[3]);
  and u_JMP (JMP, ALU_OPERATION[0], ALU_OPERATION[1], ALU_OPERATION[2], ALU_OPERATION[3]);

  // Other names for the same wires on the sheet: MEM_ID[31:0] = MEM_IN; memStore = MEM_WRITE; Save_Cmd = memWrite;
  //   OP_Code[3:0] = ALU_OPERATION

  // Notes on the sheet:
  //   INSTRUCTION MODULE
  //   CR MODULE
  //   REGISTER FILE MODULE
  //   ALU MODULE
  //   MEMORY MODULE
  //   This Could Be Wrong
  //   Control
  //   Can REG write?
  //   Is this  set CQ command?
endmodule
